# Fritzing sketch CapacitiveMoistureSensorCurrrent (saved by Fritzing 0.9.4)

parts:
  Q1 = NPN-Transistor [package="TO92 [THT]"]
  M1 = DC Motor
  U1 = NodeMCU V3.0
  Capacitive_Soil_Moisture_Sensor1 = DFRobot Capacitive Soil Moisture Sensor V1.0 [part_number=SEN0193]

nets:
  N1: Q1.E, U1.D6
  N2: Q1.B, M1.pin_1
  GND: Q1.C, U1.GND, Capacitive_Soil_Moisture_Sensor1.GND
  3V3: M1.pin_2, U1.3V3, Capacitive_Soil_Moisture_Sensor1.VCC
  N3: U1.A0, Capacitive_Soil_Moisture_Sensor1.A

custom parts:
  NodeMCU V3.0: ESP8266 based NodeMCU
  DFRobot Capacitive Soil Moisture Sensor V1.0: DFRobot Capacitive Soil Moisture Sensor V1.0 This product measures soil moisture levels by capacitive sensing, rather than resistive sensing like other types of moisture sensor. It is made of a corrosion resistant material giving it a long service life. Insert it into soil and impress your friends with the real-time soil moisture data! The product includes an on-board voltage regulator which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
