# Fritzing sketch ResistiveMoistureSensorCurrrent (saved by Fritzing 0.9.4)

parts:
  Q1 = NPN-Transistor [package="TO92 [THT]"]
  M1 = DC Motor
  U1 = NodeMCU V3.0
  Part1 = FC-28 Soil Hygrometer Module
  Part2 = FC-28 Soil Hygrometer Module - Probe

nets:
  N1: Q1.E, U1.D6
  N2: Q1.B, M1.pin_1
  GND: Q1.C, U1.GND, Part1.GND
  N3: M1.pin_2, U1.3V3
  N4: U1.D5, Part1.DO
  N5: U1.D7, Part1.VCC
  N6: U1.A0, Part1.AO
  N7: Part1.POS, Part2.POS
  N8: Part1.NEG, Part2.NEG

custom parts:
  NodeMCU V3.0: ESP8266 based NodeMCU
  FC-28 Soil Hygrometer Module: The FC-28 is a soil hygrometer module that uses the Texas Instruments LM393 comparator chip to provide an analog measurement of soil humidity. The digital output is high when soil moisture is over a certain threshold, as determined by adjusting the potentiometer.
  FC-28 Soil Hygrometer Module - Probe: The FC-28 is a soil hygrometer module that uses the Texas Instruments LM393 comparator chip to provide an analog measurement of soil humidity.
