# Fritzing sketch CapacitiveMoistureSensorCurrrent (saved by Fritzing 0.9.3b)

parts:
  M1 = DC Motor  # not connected
  U1 = NodeMCU V3.0
  Capacitive_Soil_Moisture_Sensor1 = DFRobot Capacitive Soil Moisture Sensor V1.0 [part_number=SEN0193]
  RHT1 = Humidity and Temperature Sensor RHT03
  WeMos_D1_Mini_Relay_Shield_V1 = WeMos D1 Mini Relay Shield V2
  VCC1 = Battery  # not connected

nets:
  N1: U1.D1, Capacitive_Soil_Moisture_Sensor1.VCC
  N2: U1.D2, RHT1.Data-signal
  N3: U1.D3, RHT1.Vcc
  GND: U1.GND, Capacitive_Soil_Moisture_Sensor1.GND, RHT1.GND_1, WeMos_D1_Mini_Relay_Shield_V1.G
  N4: U1.D6, WeMos_D1_Mini_Relay_Shield_V1.D0
  3V3: U1.3V3, WeMos_D1_Mini_Relay_Shield_V1.3V3
  N5: U1.A0, Capacitive_Soil_Moisture_Sensor1.A

custom parts:
  NodeMCU V3.0: ESP8266 based NodeMCU
  DFRobot Capacitive Soil Moisture Sensor V1.0: DFRobot Capacitive Soil Moisture Sensor V1.0 This product measures soil moisture levels by capacitive sensing, rather than resistive sensing like other types of moisture sensor. It is made of a corrosion resistant material giving it a long service life. Insert it into soil and impress your friends with the real-time soil moisture data! The product includes an on-board voltage regulator which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
